# Fritzing sketch hexLightboxController (saved by Fritzing 1.0.0rc)
breadboards: 1

parts:
  A1 = Particle - Photon2
  RFID_READER = RFID RC522 SIP - 8 pins [chip_label="RFID RC522" package="SIP (Single Inline) [THT]"]
  M1 = BMP280
  Red_Button = Arcade Button (red)
  Sensor1 = Gas Sensor Breakout Board
  OLED1 = OLED 128x64 I2C Monochrome Display
  80_NeoPixels = Neopixel Strip -- Black (60/m) [part_number=WS2812B]
  Green_Button_LED = smd LED [color="Green (565nm)" package="0805 [SMD]"]
  Green_Button = Arcade Button (green)

nets:
  VCC: A1.Pin_2, RFID_READER.VCC, M1.VIN, OLED1.VDD
  GND: A1.Pin_4, A1.Pin_35, RFID_READER.GND, M1.GND, Red_Button.no_name_yet#1, Sensor1.GND, OLED1.GND, 80_NeoPixels.GND, Green_Button_LED.cathode, Green_Button.no_name_yet#1
  N1: A1.Pin_5, Sensor1.AOUT
  N2: A1.Pin_7, Green_Button_LED.anode
  N3: A1.Pin_10, RFID_READER.NSS
  N4: A1.Pin_11, RFID_READER.SCK
  N5: A1.Pin_12, RFID_READER.MOSI
  N6: A1.Pin_13, RFID_READER.MISO
  N7: A1.Pin_17, M1.SDA, OLED1.SDA
  N8: A1.Pin_18, M1.SCL, OLED1.SCK
  N9: A1.Pin_19, 80_NeoPixels.DI
  N10: A1.Pin_24, Red_Button.no_name_yet#2
  N11: A1.Pin_25, Green_Button.no_name_yet#2
  5V: A1.Pin_26, Sensor1.5V, 80_NeoPixels.+5V

custom parts:
  Particle - Photon2: The Photon 2 is a microcontroller and Wi-Fi networking developed by particle. Features: 802.11a/b/g/n Wi-Fi, 2.4 GHz and 5 GHz Integrated PCB antenna Integrated U.FL connector for external antenna Integrated RF switch BLE 5 using same antenna as Wi-Fi Realtek RTL8721DM MCU ARM Cortex M33 CPU, 200 MHz 2048 KB (2 MB) user application maximum size 3072 KB (3 MB) of RAM available to user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
  RFID RC522 SIP - 8 pins: A SIP stand-in part for RFID RC522 . With 8 pins on a 300 mil single inline package (SIP) footprint.
  BMP280: Temperature Humidity Barometric presure Sensor, I2C
  Arcade Button (red): Adafruit Arcade Button (red)
  Gas Sensor Breakout Board: Gas sensor breakout board. Input voltage is 5V. Sensor output is available in analog and digital.
  Neopixel Strip -- Black (60/m): Neopixel Strip, Black, 60 pixels per meter.
  Arcade Button (green): Adafruit Arcade Button (green)
